# Fritzing sketch postur_tracking_system (saved by Fritzing 0.9.5d)
breadboards: 1

parts:
  flex = Basic Flex Resistor
  imu1 = InvenSense MPU6050
  imu2 = InvenSense MPU6050
  button = Pushbutton [package="[THT]"]
  ardunio_uno = Arduino Uno (Rev3)
  10k_direnç = Resistor [tolerance=±5% resistance=10k package="2512 [SMD]"]
  buzzer = Buzzer 12mm [package=buzzer-12mm]

nets:
  N1: flex.Pin_2, ardunio_uno.A0, 10k_direnç.Pin_1
  VCC: flex.pin_1, imu1.VCC, imu2.VCC, imu2.AD0, ardunio_uno.5V
  GND: imu1.GND, imu1.AD0, imu2.GND, button.Pin_3, button.Pin_4, ardunio_uno.GND, 10k_direnç.Pin_0, buzzer.1
  N2: imu1.SCL, imu2.SCL, ardunio_uno.A5/SCL
  N3: imu1.SDA, imu2.SDA, ardunio_uno.A4/SDA
  N4: button.Pin_1, button.Pin_2, ardunio_uno.D7
  N5: ardunio_uno.D8, buzzer.2

notes:
  FLEX SENSOR
  1-mpu6050(imu sensor)
  2-mpu6050(imu sensor)
  BUZZER
  button

// code stored in the sketch: Untitled.ino
#include <Wire.h>
#include <MPU6050.h>

MPU6050 mpu1(0x68);
MPU6050 mpu2(0x69);

// MPU verileri
int16_t ax1, ay1, az1;
int16_t ax2, ay2, az2;

float pitch1 = 0;
float pitch2 = 0;
float diff = 0;
float smoothDiff = 0;

// Pinler
const int flexPin = A0;
const int buzzerPin = 8;
const int buttonPin = 7;

// Flex
int flexValue = 0;

// Kalibrasyon
float baseDiff = 0;
int baseFlex = 0;
bool calibrated = false;

// Stabilite
int stableCount = 0;
bool isBad = false;

// E?ikler
const float CALIB_DIFF_LIMIT = 18.0;   // Kalibrasyon için maksimum MPU fark?
const int FLEX_MIN_LIMIT = 250;        // Flex minimum kabul de?eri
const int FLEX_MAX_LIMIT = 900;        // Flex maksimum kabul de?eri

const float BAD_DIFF_LIMIT = 10.0;
const float VERY_BAD_DIFF_LIMIT = 18.0;

const int BAD_FLEX_LIMIT = 25;
const int VERY_BAD_FLEX_LIMIT = 40;

void setup() {
  Serial.begin(9600);
  Wire.begin();

  mpu1.initialize();
  mpu2.initialize();

  pinMode(flexPin, INPUT);
  pinMode(buzzerPin, OUTPUT);
  pinMode(buttonPin, INPUT_PULLUP);

  delay(1000);

  Serial.println("Postur Takip Sistemi Basladi");

  if (!mpu1.testConnection()) {
    Serial.println("HATA: MPU1 baglantisi yok! 0x68 kontrol et.");
    errorBeep();
  } else {
    Serial.println("MPU1 baglandi.");
  }

  if (!mpu2.testConnection()) {
    Serial.println("HATA: MPU2 baglantisi yok! 0x69 kontrol et.");
    errorBeep();
  } else {
    Serial.println("MPU2 baglandi.");
  }

  Serial.println("Dik dur ve kalibrasyon icin butona bas.");
}

void loop() {
  readSensors();

  if (!calibrated) {
    Serial.print("Kalibrasyon bekleniyor | Diff: ");
    Serial.print(diff);
    Serial.print(" | Flex: ");
    Serial.println(flexValue);

    if (buttonPressed()) {
      Serial.println("Butona basildi. Kalibrasyon kontrol ediliyor...");

      if (isCalibrationPositionValid()) {
        successBeepShort();

        Serial.println("Kalibrasyon basliyor. 2 saniye hareket etme...");
        calibrateSystem();

        calibrated = true;
        smoothDiff = baseDiff;

        Serial.print("Kalibrasyon tamamlandi | BaseDiff: ");
        Serial.print(baseDiff);
        Serial.print(" | BaseFlex: ");
        Serial.println(baseFlex);

        successBeepLong();
      } 
      else {
        Serial.println("Kalibrasyon reddedildi!");
        Serial.println("Daha dik dur veya sensorleri kontrol et.");
        errorBeep();
      }

      delay(700);
    }

    delay(300);
    return;
  }

  // Filtre
  smoothDiff = 0.8 * smoothDiff + 0.2 * diff;

  float diffError = abs(smoothDiff - baseDiff);
  int flexError = abs(baseFlex - flexValue);

  // Stabilite kontrolü
  if (diffError > BAD_DIFF_LIMIT || flexError > BAD_FLEX_LIMIT) {
    stableCount++;
  } else {
    stableCount = 0;
  }

  isBad = stableCount > 3;

  // Karar
  if (diffError > VERY_BAD_DIFF_LIMIT && flexError > VERY_BAD_FLEX_LIMIT) {
    Serial.println("VERY BAD POSTURE");
    tone(buzzerPin, 2000);
  }
  else if (isBad) {
    Serial.println("BAD POSTURE");

    tone(buzzerPin, 1000);
    delay(100);
    noTone(buzzerPin);
    delay(100);
  }
  else {
    Serial.println("GOOD POSTURE");
    noTone(buzzerPin);
  }

  Serial.print("DiffErr: ");
  Serial.print(diffError);
  Serial.print(" | FlexErr: ");
  Serial.print(flexError);
  Serial.print(" | Diff: ");
  Serial.print(diff);
  Serial.print(" | Flex: ");
  Serial.println(flexValue);

  delay(100);
}

void readSensors() {
  // MPU1
  mpu1.getAcceleration(&ax1, &ay1, &az1);
  float AccX1 = ax1 / 16384.0;
  float AccY1 = ay1 / 16384.0;
  float AccZ1 = az1 / 16384.0;

  pitch1 = atan2(AccX1, sqrt(AccY1 * AccY1 + AccZ1 * AccZ1)) * 180 / PI;

  // MPU2
  mpu2.getAcceleration(&ax2, &ay2, &az2);
  float AccX2 = ax2 / 16384.0;
  float AccY2 = ay2 / 16384.0;
  float AccZ2 = az2 / 16384.0;

  pitch2 = atan2(AccX2, sqrt(AccY2 * AccY2 + AccZ2 * AccZ2)) * 180 / PI;

  diff = pitch1 - pitch2;

  flexValue = analogRead(flexPin);
}

bool isCalibrationPositionValid() {
  readSensors();

  Serial.print("Kontrol Diff: ");
  Serial.print(diff);
  Serial.print(" | Flex: ");
  Serial.println(flexValue);

  if (abs(diff) > CALIB_DIFF_LIMIT) {
    return false;
  }

  if (flexValue < FLEX_MIN_LIMIT || flexValue > FLEX_MAX_LIMIT) {
    return false;
  }

  return true;
}

void calibrateSystem() {
  float sumDiff = 0;
  long sumFlex = 0;

  for (int i = 0; i < 100; i++) {
    readSensors();

    sumDiff += diff;
    sumFlex += flexValue;

    delay(20);
  }

  baseDiff = sumDiff / 100.0;
  baseFlex = sumFlex / 100;
}

bool buttonPressed() {
  if (digitalRead(buttonPin) == LOW) {
    delay(30);

    if (digitalRead(buttonPin) == LOW) {
      while (digitalRead(buttonPin) == LOW) {
        delay(10);
      }

      return true;
    }
  }

  return false;
}

void successBeepShort() {
  tone(buzzerPin, 1500);
  delay(150);
  noTone(buzzerPin);
}

void successBeepLong() {
  tone(buzzerPin, 2000);
  delay(400);
  noTone(buzzerPin);
}

void errorBeep() {
  tone(buzzerPin, 400);
  delay(500);
  noTone(buzzerPin);
}
